# Fritzing sketch Tugas Besar Sch (saved by Fritzing 0.8.7b)
breadboards: 1

parts:
  Part1 = SRF05 Ultrasonic Rangefinder
  Part2 = Arduino Uno (Rev3)
  KY-1 = Keyes Relay [package=THT]
  LED1 = LEDs [package=led10mm]
  Part3 = LilyPad Slide Switch

nets:
  VCC: Part1.VCC, Part2.5V, KY-1.power
  GND: Part1.Trig, Part1.GND, Part2.D9_PWM, Part2.D7, Part2.GND, KY-1.signal, KY-1.ground
  N1: Part1.Echo, Part2.D10_PWM/SS
  N2: KY-1.C, Part3.OFF
  N3: KY-1.NO, LED1.C
  N4: LED1.A, Part3.ON

custom parts:
  Keyes Relay: The Keyes 5V relay module is suitable for SCM development, home appliance control. It uses a 5V~12V TIL control signal which can control DC / AC signal.
  LEDs: LEDs Standard schematic elements and footprints for 5mm, 3mm, 1206, and 0603 sized LEDs. 5mm - Spark Fun Electronics SKU : COM-00529 (and others)
